// Logisim project Processor.circ as structural Verilog: 2 circuits, main circuit main
module main (
);

  ULA ula_1 ();  // open: _1_4, _2_4, _4_4, _8_3, _16_3, _32_3, _64_3, _128_3, _128, _64, _32, _16, _8, _4, _2, _1, _4_3, _2_3, _128_2, _1_3, _64_2, _32_2, _16_2, _8_2, _4_2, _2_2, _1_2
endmodule

module ULA (
  input  _128,
  input  _64,
  input  _32,
  input  _16,
  input  _8,
  input  _4,
  input  _2,
  input  _1,
  input  _128_2,
  input  _64_2,
  input  _32_2,
  input  _16_2,
  input  _8_2,
  input  _4_2,
  input  _2_2,
  input  _1_2,
  input  _4_3,
  input  _2_3,
  input  _1_3,
  output _1_4,
  output _2_4,
  output _4_4,
  output _8_3,
  output _16_3,
  output _32_3,
  output _64_3,
  output _128_3
);

  wire [7:0] adder_1_out, adder_2_out, adder_3_out, and_1_out, or_1_out, subtractor_1_out;

  Adder adder_1 (.a({_128, _64, _32, _16, _8, _4, _2, _1}), .b(8'h1), .out(adder_1_out));  // open: cin, cout
  Adder adder_2 (
    .a({_128_2, _64_2, _32_2, _16_2, _8_2, _4_2, _2_2, _1_2}), .b(8'h1), .out(adder_2_out));  // open: cin, cout
  Adder adder_3 (
    .a({_128, _64, _32, _16, _8, _4, _2, _1}), .b({_128_2, _64_2, _32_2, _16_2, _8_2, _4_2, _2_2, _1_2}),
    .out(adder_3_out));  // open: cin, cout
  Subtractor subtractor_1 (
    .a({_128, _64, _32, _16, _8, _4, _2, _1}), .b({_128_2, _64_2, _32_2, _16_2, _8_2, _4_2, _2_2, _1_2}),
    .out(subtractor_1_out));  // open: bin, bout
  assign and_1_out = {_128, _64, _32, _16, _8, _4, _2, _1} & {_128_2, _64_2, _32_2, _16_2, _8_2, _4_2, _2_2, _1_2};  // AND_Gate and_1, 8 bits wide
  assign or_1_out = {_128, _64, _32, _16, _8, _4, _2, _1} | {_128_2, _64_2, _32_2, _16_2, _8_2, _4_2, _2_2, _1_2};  // OR_Gate or_1, 8 bits wide
  Multiplexer #(.select(3), .width(8)) multiplexer_1 (
    .in0({_128, _64, _32, _16, _8, _4, _2, _1}), .in1({_128_2, _64_2, _32_2, _16_2, _8_2, _4_2, _2_2, _1_2}),
    .in2(adder_1_out), .in3(adder_2_out), .in4(adder_3_out), .in5(subtractor_1_out), .in6(and_1_out),
    .in7(or_1_out), .out({_128_3, _64_3, _32_3, _16_3, _8_3, _4_4, _2_4, _1_4}), .sel({_4_3, _2_3, _1_3}));  // open: en
endmodule
